# Fritzing sketch 6502 clean (saved by Fritzing 0.9.3b)
circuit board: 8.46667cm x 5.64444cm
breadboards: 5

parts:
  65C02 = WDC 65C02 [package="DIP (Dual Inline) [THT]"]
  R1 = Resistor [tolerance=±5% resistance=10k package=THT]
  R2 = Resistor [tolerance=±5% resistance=10k package=THT]
  R3 = Resistor [tolerance=±5% resistance=10k package=THT]
  R4 = Resistor [tolerance=±5% resistance=10k package=THT]
  S1 = Pushbutton [package="[THT]"]
  Teensy1 = Teensy 3.6 (Basic)

nets:
  N1: 65C02.RDY', R2.Pin_1
  N2: 65C02.IRQB, R3.Pin_1
  N3: 65C02.NMIB, R4.Pin_1
  VDD: 65C02.VDD, 65C02.RESB, R1.Pin_1, R2.Pin_0, R3.Pin_0, R4.Pin_0, S1.Pin_3, S1.Pin_4, Teensy1.3V3, Teensy1.3V3_1
  N4: 65C02.A0, Teensy1.A1/D15
  N5: 65C02.A1, Teensy1.A8/D22
  N6: 65C02.A2, Teensy1.A9/D23
  N7: 65C02.A3, Teensy1.D9
  N8: 65C02.A4, Teensy1.D10
  N9: 65C02.A5, Teensy1.D13
  N10: 65C02.A6, Teensy1.D11
  N11: 65C02.A7, Teensy1.D12
  N12: 65C02.A8, Teensy1.A2/D16
  N13: 65C02.A9, Teensy1.A3/D17
  N14: 65C02.A10, Teensy1.A5/D19
  N15: 65C02.A11, Teensy1.A4/D18
  VSS: 65C02.VSS, S1.Pin_1, S1.Pin_2, Teensy1.GND, Teensy1.GND1
  N16: 65C02.A12, Teensy1.D0
  N17: 65C02.A13, Teensy1.D1
  N18: 65C02.A14, Teensy1.D29
  N19: 65C02.A15, Teensy1.D30
  N20: 65C02.D7, Teensy1.D5
  N21: 65C02.D6, Teensy1.A7/D21
  N22: 65C02.D5, Teensy1.A6/D20
  N23: 65C02.D4, Teensy1.D6
  N24: 65C02.D3, Teensy1.D8
  N25: 65C02.D2, Teensy1.D7
  N26: 65C02.D1, Teensy1.A0/D14
  N27: 65C02.D0, Teensy1.D2
  N28: 65C02.BE, R1.Pin_0
  N29: 65C02.PHI2, Teensy1.D3

custom parts:
  WDC 65C02: A standard 65C02 from WDC in DIP format
  Teensy 3.6 (Basic): The Teensy is a complete USB-based microcontoller development system, in a very small footprint, capable of implementing many types of projects. All programming is done via the USB port. No special programmer is needed, only a standard micro-USB cable and a PC or Macintosh with a USB port.
