# Fritzing sketch SBC v0.5 2 (saved by Fritzing 0.9.3b)
breadboards: 2

parts:
  Teensy1 = Teensy 3.6 (Basic)
  WDC65C1 = WDC65C02 [package="DIP (Dual Inline) [THT]"]
  VCC1 = Battery
  R1 = Resistor [tolerance=±5% resistance=10k package=THT]
  R2 = Resistor [tolerance=±5% resistance=10k package=THT]
  R3 = Resistor [tolerance=±5% resistance=10k package=THT]
  R4 = Resistor [tolerance=±5% resistance=10k package=THT]
  S1 = Pushbutton [package="[THT]"]

nets:
  GND: Teensy1.GND, Teensy1.GND1, WDC65C1.VSS, VCC1.-, S1.Pin_1, S1.Pin_2
  N1: Teensy1.D0, WDC65C1.A12
  N2: Teensy1.D1, WDC65C1.A13
  N3: Teensy1.D2, WDC65C1.D0
  N4: Teensy1.D3, WDC65C1.RWB
  N5: Teensy1.D4, WDC65C1.PHI2
  N6: Teensy1.D5, WDC65C1.D7
  N7: Teensy1.D6, WDC65C1.D4
  N8: Teensy1.D7, WDC65C1.D2
  N9: Teensy1.D8, WDC65C1.D3
  N10: Teensy1.D9, WDC65C1.A3
  N11: Teensy1.D10, WDC65C1.A4
  N12: Teensy1.D11, WDC65C1.A6
  N13: Teensy1.D12, WDC65C1.A7
  N14: Teensy1.D13, WDC65C1.A5
  N15: Teensy1.A0/D14, WDC65C1.D1
  N16: Teensy1.A1/D15, WDC65C1.A0
  N17: Teensy1.A2/D16, WDC65C1.A8
  N18: Teensy1.A3/D17, WDC65C1.A9
  N19: Teensy1.A4/D18, WDC65C1.A11
  N20: Teensy1.A5/D19, WDC65C1.A10
  N21: Teensy1.A6/D20, WDC65C1.D5
  N22: Teensy1.A7/D21, WDC65C1.D6
  N23: Teensy1.A8/D22, WDC65C1.A1
  N24: Teensy1.A9/D23, WDC65C1.A2
  N25: Teensy1.3V3, Teensy1.3V3_1
  N26: Teensy1.D29, WDC65C1.A14
  N27: Teensy1.D30, WDC65C1.A15
  N28: Teensy1.D33, WDC65C1.RESB, S1.Pin_3, S1.Pin_4
  N29: WDC65C1.RDY, R1.Pin_0
  N30: WDC65C1.IRQB, R2.Pin_0
  N31: WDC65C1.NMIB, R3.Pin_0
  N32: WDC65C1.VDD, VCC1.+, R1.Pin_1, R2.Pin_1, R3.Pin_1, R4.Pin_0
  N33: WDC65C1.BE, R4.Pin_1

custom parts:
  Teensy 3.6 (Basic): The Teensy is a complete USB-based microcontoller development system, in a very small footprint, capable of implementing many types of projects. All programming is done via the USB port. No special programmer is needed, only a standard micro-USB cable and a PC or Macintosh with a USB port.
  WDC65C02: The W65C02S is a low power cost sensitive 8-bit microprocessor. The W65C02S is a fully static core and the PHI2 clock can be stopped when it is in the high (logic 1) or low (logic 0) state. The variable length instruction set and manually optimized core size makes the W65C02S an excellent choice for low power System-on-Chip (SoC) designs. The Verilog RTL model is available for ASIC design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
